// Logisim project 2101CS90.circ as structural Verilog
module E1 (
  input  in_1,
  output out_2
);

  wire clock_1_out, d_ff_1_q, d_ff_2_q, d_ff_3_q, d_ff_4_q;

  Clock clock_1 (.out(clock_1_out));
  D_Flip_Flop d_ff_1 (.clk(clock_1_out), .D(in_1), .Q(d_ff_1_q));  // open: Qn, preset, en, reset
  D_Flip_Flop d_ff_2 (.clk(clock_1_out), .D(d_ff_1_q), .Q(d_ff_2_q));  // open: Qn, preset, en, reset
  D_Flip_Flop d_ff_3 (.clk(clock_1_out), .D(d_ff_2_q), .Q(d_ff_3_q));  // open: Qn, preset, en, reset
  D_Flip_Flop d_ff_4 (.clk(clock_1_out), .D(d_ff_3_q), .Q(d_ff_4_q));  // open: Qn, preset, en, reset
  D_Flip_Flop d_ff_5 (.clk(clock_1_out), .D(d_ff_4_q), .Q(out_2));  // open: Qn, preset, en, reset
endmodule

module E2 (
  input  in_1,
  output out_2,
  output out_3,
  output out_4,
  output out_5
);

  wire clock_1_out;

  Clock clock_1 (.out(clock_1_out));
  T_Flip_Flop t_ff_1 (.clk(clock_1_out), .T(in_1), .Q(out_2));  // open: Qn, preset, reset, en
  T_Flip_Flop t_ff_2 (.clk(out_2), .T(in_1), .Q(out_3));  // open: Qn, preset, reset, en
  T_Flip_Flop t_ff_3 (.clk(out_3), .T(in_1), .Q(out_4));  // open: Qn, preset, reset, en
  Hex_Digit_Display hex_digit_display_1 (.value({out_5, out_4, out_3, out_2}));  // open: dp
  T_Flip_Flop t_ff_4 (.clk(out_4), .T(in_1), .Q(out_5));  // open: Qn, preset, reset, en
endmodule

module _5bit_pipo_Register_for_E3 (
  input  in_1,
  input  in_2,
  input  in_3,
  input  in_4,
  input  in_5,
  input  Clock,
  output out_7,
  output out_8,
  output out_9,
  output out_10,
  output out_11
);

  D_Flip_Flop d_ff_1 (.clk(Clock), .D(in_1), .Q(out_7));  // open: Qn, preset, en, reset
  D_Flip_Flop d_ff_2 (.clk(Clock), .D(in_2), .Q(out_8));  // open: Qn, preset, en, reset
  D_Flip_Flop d_ff_3 (.clk(Clock), .D(in_3), .Q(out_9));  // open: Qn, preset, en, reset
  D_Flip_Flop d_ff_4 (.clk(Clock), .D(in_4), .Q(out_10));  // open: Qn, preset, en, reset
  D_Flip_Flop d_ff_5 (.clk(Clock), .D(in_5), .Q(out_11));  // open: Qn, preset, en, reset
endmodule

module E3 (
  input  in_1,
  input  in_2,
  input  in_3,
  input  in_4,
  input  in_5,
  output out_6,
  output out_7,
  output out_8,
  output out_9,
  output out_10,
  output out_11,
  output out_12,
  output out_13,
  output out_14,
  output out_15,
  output out_16,
  output out_17,
  output out_18,
  output out_19,
  output out_20
);

  wire clock_1_out;

  _5bit_pipo_Register_for_E3 u_5bit_pipo_register_for_e3_1 (
    .in_1(in_1), .in_2(in_2), .in_3(in_3), .in_4(in_4), .in_5(in_5), .out_7(out_6), .out_8(out_7),
    .out_9(out_8), .out_10(out_9), .out_11(out_10), .Clock(clock_1_out));
  Clock clock_1 (.out(clock_1_out));
  _5bit_pipo_Register_for_E3 u_5bit_pipo_register_for_e3_2 (
    .in_1(out_6), .in_2(out_7), .in_3(out_8), .in_4(out_9), .in_5(out_10), .out_7(out_11), .out_8(out_12),
    .out_9(out_13), .out_10(out_14), .out_11(out_15), .Clock(clock_1_out));
  _5bit_pipo_Register_for_E3 u_5bit_pipo_register_for_e3_3 (
    .in_1(out_11), .in_2(out_12), .in_3(out_13), .in_4(out_14), .in_5(out_15), .out_7(out_16),
    .out_8(out_17), .out_9(out_18), .out_10(out_19), .out_11(out_20), .Clock(clock_1_out));
endmodule

module E4 (
  input  in_1,
  input  in_2,
  output out_3,
  output out_4,
  output out_5,
  output out_6
);

  wire clock_1_out, inverter_1_p2, multiplexer_1_out, multiplexer_2_out, multiplexer_3_out, multiplexer_4_out;

  Clock clock_1 (.out(clock_1_out));
  // Inverter inverter_1: pin names not known; wires that end beside it: in_1, inverter_1_p2
  Multiplexer multiplexer_1 (.in0(in_2), .in1(out_3), .out(multiplexer_1_out), .sel(inverter_1_p2));  // open: en
  Multiplexer multiplexer_2 (.in0(out_3), .in1(out_4), .out(multiplexer_2_out), .sel(inverter_1_p2));  // open: en
  D_Flip_Flop d_ff_1 (.clk(clock_1_out), .D(multiplexer_1_out), .Q(out_3));  // open: Qn, preset, en, reset
  D_Flip_Flop d_ff_2 (.clk(clock_1_out), .D(multiplexer_2_out), .Q(out_4));  // open: Qn, preset, en, reset
  Multiplexer multiplexer_3 (.in0(out_4), .in1(out_5), .out(multiplexer_3_out), .sel(inverter_1_p2));  // open: en
  D_Flip_Flop d_ff_3 (.clk(clock_1_out), .D(multiplexer_3_out), .Q(out_5));  // open: Qn, preset, en, reset
  Multiplexer multiplexer_4 (.in0(out_5), .in1(out_6), .out(multiplexer_4_out), .sel(inverter_1_p2));  // open: en
  D_Flip_Flop d_ff_4 (.clk(clock_1_out), .D(multiplexer_4_out), .Q(out_6));  // open: Qn, preset, en, reset
endmodule

module E5 (
  input  [7:0] in_1,
  input  [2:0] in_2,
  input  [2:0] in_3,
  output [7:0] out_4
);

  wire clock_1_out, decoder_1_out0, decoder_1_out1, decoder_1_out2, decoder_1_out3, decoder_1_out4,
       decoder_1_out5, decoder_1_out6, decoder_1_out7;
  wire [7:0] d_ff_57_q, d_ff_58_q, d_ff_59_q, d_ff_60_q, d_ff_61_q, d_ff_62_q, d_ff_63_q, d_ff_64_q;

  Clock clock_1 (.out(clock_1_out));
  Decoder #(.select(3)) decoder_1 (
    .out0(decoder_1_out0), .out1(decoder_1_out1), .out2(decoder_1_out2), .out3(decoder_1_out3),
    .out4(decoder_1_out4), .out5(decoder_1_out5), .out6(decoder_1_out6), .out7(decoder_1_out7), .sel(in_2));  // open: en
  D_Flip_Flop d_ff_1 (
    .clk(clock_1_out), .D(in_1[7]), .Q(d_ff_57_q[7]), .en(decoder_1_out0));  // open: Qn, preset, reset
  D_Flip_Flop d_ff_2 (.clk(clock_1_out), .D(in_1[7]), .Q(d_ff_58_q[7]));  // open: Qn, preset, en, reset
  D_Flip_Flop d_ff_3 (
    .clk(clock_1_out), .D(in_1[7]), .Q(d_ff_59_q[7]), .en(decoder_1_out2));  // open: Qn, preset, reset
  D_Flip_Flop d_ff_4 (
    .clk(clock_1_out), .D(in_1[7]), .Q(d_ff_60_q[7]), .en(decoder_1_out3));  // open: Qn, preset, reset
  D_Flip_Flop d_ff_5 (
    .clk(clock_1_out), .D(in_1[7]), .Q(d_ff_61_q[7]), .en(decoder_1_out4));  // open: Qn, preset, reset
  D_Flip_Flop d_ff_6 (
    .clk(clock_1_out), .D(in_1[7]), .Q(d_ff_62_q[7]), .en(decoder_1_out5));  // open: Qn, preset, reset
  D_Flip_Flop d_ff_7 (
    .clk(clock_1_out), .D(in_1[7]), .Q(d_ff_63_q[7]), .en(decoder_1_out6));  // open: Qn, preset, reset
  D_Flip_Flop d_ff_8 (
    .clk(clock_1_out), .D(in_1[7]), .Q(d_ff_64_q[7]), .en(decoder_1_out7));  // open: Qn, preset, reset
  D_Flip_Flop d_ff_9 (
    .clk(clock_1_out), .D(in_1[6]), .Q(d_ff_57_q[6]), .en(decoder_1_out0));  // open: Qn, preset, reset
  D_Flip_Flop d_ff_10 (
    .clk(clock_1_out), .D(in_1[6]), .Q(d_ff_58_q[6]), .en(decoder_1_out1));  // open: Qn, preset, reset
  D_Flip_Flop d_ff_11 (
    .clk(clock_1_out), .D(in_1[6]), .Q(d_ff_59_q[6]), .en(decoder_1_out2));  // open: Qn, preset, reset
  D_Flip_Flop d_ff_12 (
    .clk(clock_1_out), .D(in_1[6]), .Q(d_ff_60_q[6]), .en(decoder_1_out3));  // open: Qn, preset, reset
  D_Flip_Flop d_ff_13 (
    .clk(clock_1_out), .D(in_1[6]), .Q(d_ff_61_q[6]), .en(decoder_1_out4));  // open: Qn, preset, reset
  D_Flip_Flop d_ff_14 (
    .clk(clock_1_out), .D(in_1[6]), .Q(d_ff_62_q[6]), .en(decoder_1_out5));  // open: Qn, preset, reset
  D_Flip_Flop d_ff_15 (
    .clk(clock_1_out), .D(in_1[6]), .Q(d_ff_63_q[6]), .en(decoder_1_out6));  // open: Qn, preset, reset
  D_Flip_Flop d_ff_16 (
    .clk(clock_1_out), .D(in_1[6]), .Q(d_ff_64_q[6]), .en(decoder_1_out7));  // open: Qn, preset, reset
  D_Flip_Flop d_ff_17 (
    .clk(clock_1_out), .D(in_1[5]), .Q(d_ff_57_q[5]), .en(decoder_1_out0));  // open: Qn, preset, reset
  D_Flip_Flop d_ff_18 (
    .clk(clock_1_out), .D(in_1[5]), .Q(d_ff_58_q[5]), .en(decoder_1_out1));  // open: Qn, preset, reset
  D_Flip_Flop d_ff_19 (
    .clk(clock_1_out), .D(in_1[5]), .Q(d_ff_59_q[5]), .en(decoder_1_out2));  // open: Qn, preset, reset
  D_Flip_Flop d_ff_20 (
    .clk(clock_1_out), .D(in_1[5]), .Q(d_ff_60_q[5]), .en(decoder_1_out3));  // open: Qn, preset, reset
  D_Flip_Flop d_ff_21 (
    .clk(clock_1_out), .D(in_1[5]), .Q(d_ff_61_q[5]), .en(decoder_1_out4));  // open: Qn, preset, reset
  D_Flip_Flop d_ff_22 (
    .clk(clock_1_out), .D(in_1[5]), .Q(d_ff_62_q[5]), .en(decoder_1_out5));  // open: Qn, preset, reset
  D_Flip_Flop d_ff_23 (
    .clk(clock_1_out), .D(in_1[5]), .Q(d_ff_63_q[5]), .en(decoder_1_out6));  // open: Qn, preset, reset
  D_Flip_Flop d_ff_24 (
    .clk(clock_1_out), .D(in_1[5]), .Q(d_ff_64_q[5]), .en(decoder_1_out7));  // open: Qn, preset, reset
  D_Flip_Flop d_ff_25 (
    .clk(clock_1_out), .D(in_1[4]), .Q(d_ff_57_q[4]), .en(decoder_1_out0));  // open: Qn, preset, reset
  D_Flip_Flop d_ff_26 (
    .clk(clock_1_out), .D(in_1[4]), .Q(d_ff_58_q[4]), .en(decoder_1_out1));  // open: Qn, preset, reset
  D_Flip_Flop d_ff_27 (
    .clk(clock_1_out), .D(in_1[4]), .Q(d_ff_59_q[4]), .en(decoder_1_out2));  // open: Qn, preset, reset
  D_Flip_Flop d_ff_28 (
    .clk(clock_1_out), .D(in_1[4]), .Q(d_ff_60_q[4]), .en(decoder_1_out3));  // open: Qn, preset, reset
  D_Flip_Flop d_ff_29 (
    .clk(clock_1_out), .D(in_1[4]), .Q(d_ff_61_q[4]), .en(decoder_1_out4));  // open: Qn, preset, reset
  D_Flip_Flop d_ff_30 (
    .clk(clock_1_out), .D(in_1[4]), .Q(d_ff_62_q[4]), .en(decoder_1_out5));  // open: Qn, preset, reset
  D_Flip_Flop d_ff_31 (
    .clk(clock_1_out), .D(in_1[4]), .Q(d_ff_63_q[4]), .en(decoder_1_out6));  // open: Qn, preset, reset
  D_Flip_Flop d_ff_32 (
    .clk(clock_1_out), .D(in_1[4]), .Q(d_ff_64_q[4]), .en(decoder_1_out7));  // open: Qn, preset, reset
  D_Flip_Flop d_ff_33 (
    .clk(clock_1_out), .D(in_1[3]), .Q(d_ff_57_q[3]), .en(decoder_1_out0));  // open: Qn, preset, reset
  D_Flip_Flop d_ff_34 (
    .clk(clock_1_out), .D(in_1[3]), .Q(d_ff_58_q[3]), .en(decoder_1_out1));  // open: Qn, preset, reset
  D_Flip_Flop d_ff_35 (
    .clk(clock_1_out), .D(in_1[3]), .Q(d_ff_59_q[3]), .en(decoder_1_out2));  // open: Qn, preset, reset
  D_Flip_Flop d_ff_36 (
    .clk(clock_1_out), .D(in_1[3]), .Q(d_ff_60_q[3]), .en(decoder_1_out3));  // open: Qn, preset, reset
  D_Flip_Flop d_ff_37 (
    .clk(clock_1_out), .D(in_1[3]), .Q(d_ff_61_q[3]), .en(decoder_1_out4));  // open: Qn, preset, reset
  D_Flip_Flop d_ff_38 (
    .clk(clock_1_out), .D(in_1[3]), .Q(d_ff_62_q[3]), .en(decoder_1_out5));  // open: Qn, preset, reset
  D_Flip_Flop d_ff_39 (
    .clk(clock_1_out), .D(in_1[3]), .Q(d_ff_63_q[3]), .en(decoder_1_out6));  // open: Qn, preset, reset
  D_Flip_Flop d_ff_40 (
    .clk(clock_1_out), .D(in_1[3]), .Q(d_ff_64_q[3]), .en(decoder_1_out7));  // open: Qn, preset, reset
  D_Flip_Flop d_ff_41 (
    .clk(clock_1_out), .D(in_1[2]), .Q(d_ff_57_q[2]), .en(decoder_1_out0));  // open: Qn, preset, reset
  D_Flip_Flop d_ff_42 (
    .clk(clock_1_out), .D(in_1[2]), .Q(d_ff_58_q[2]), .en(decoder_1_out1));  // open: Qn, preset, reset
  D_Flip_Flop d_ff_43 (
    .clk(clock_1_out), .D(in_1[2]), .Q(d_ff_59_q[2]), .en(decoder_1_out2));  // open: Qn, preset, reset
  D_Flip_Flop d_ff_44 (
    .clk(clock_1_out), .D(in_1[2]), .Q(d_ff_60_q[2]), .en(decoder_1_out3));  // open: Qn, preset, reset
  D_Flip_Flop d_ff_45 (
    .clk(clock_1_out), .D(in_1[2]), .Q(d_ff_61_q[2]), .en(decoder_1_out4));  // open: Qn, preset, reset
  D_Flip_Flop d_ff_46 (
    .clk(clock_1_out), .D(in_1[2]), .Q(d_ff_62_q[2]), .en(decoder_1_out5));  // open: Qn, preset, reset
  D_Flip_Flop d_ff_47 (
    .clk(clock_1_out), .D(in_1[2]), .Q(d_ff_63_q[2]), .en(decoder_1_out6));  // open: Qn, preset, reset
  D_Flip_Flop d_ff_48 (
    .clk(clock_1_out), .D(in_1[2]), .Q(d_ff_64_q[2]), .en(decoder_1_out7));  // open: Qn, preset, reset
  D_Flip_Flop d_ff_49 (
    .clk(clock_1_out), .D(in_1[1]), .Q(d_ff_57_q[1]), .en(decoder_1_out0));  // open: Qn, preset, reset
  D_Flip_Flop d_ff_50 (
    .clk(clock_1_out), .D(in_1[1]), .Q(d_ff_58_q[1]), .en(decoder_1_out1));  // open: Qn, preset, reset
  D_Flip_Flop d_ff_51 (
    .clk(clock_1_out), .D(in_1[1]), .Q(d_ff_59_q[1]), .en(decoder_1_out2));  // open: Qn, preset, reset
  D_Flip_Flop d_ff_52 (
    .clk(clock_1_out), .D(in_1[1]), .Q(d_ff_60_q[1]), .en(decoder_1_out3));  // open: Qn, preset, reset
  D_Flip_Flop d_ff_53 (
    .clk(clock_1_out), .D(in_1[1]), .Q(d_ff_61_q[1]), .en(decoder_1_out4));  // open: Qn, preset, reset
  D_Flip_Flop d_ff_54 (
    .clk(clock_1_out), .D(in_1[1]), .Q(d_ff_62_q[1]), .en(decoder_1_out5));  // open: Qn, preset, reset
  D_Flip_Flop d_ff_55 (
    .clk(clock_1_out), .D(in_1[1]), .Q(d_ff_63_q[1]), .en(decoder_1_out6));  // open: Qn, preset, reset
  D_Flip_Flop d_ff_56 (
    .clk(clock_1_out), .D(in_1[1]), .Q(d_ff_64_q[1]), .en(decoder_1_out7));  // open: Qn, preset, reset
  D_Flip_Flop d_ff_57 (
    .clk(clock_1_out), .D(in_1[0]), .Q(d_ff_57_q[0]), .en(decoder_1_out0));  // open: Qn, preset, reset
  D_Flip_Flop d_ff_58 (
    .clk(clock_1_out), .D(in_1[0]), .Q(d_ff_58_q[0]), .en(decoder_1_out1));  // open: Qn, preset, reset
  D_Flip_Flop d_ff_59 (
    .clk(clock_1_out), .D(in_1[0]), .Q(d_ff_59_q[0]), .en(decoder_1_out2));  // open: Qn, preset, reset
  D_Flip_Flop d_ff_60 (
    .clk(clock_1_out), .D(in_1[0]), .Q(d_ff_60_q[0]), .preset(decoder_1_out3), .en(decoder_1_out3));  // open: Qn, reset
  D_Flip_Flop d_ff_61 (
    .clk(clock_1_out), .D(in_1[0]), .Q(d_ff_61_q[0]), .en(decoder_1_out4));  // open: Qn, preset, reset
  D_Flip_Flop d_ff_62 (
    .clk(clock_1_out), .D(in_1[0]), .Q(d_ff_62_q[0]), .en(decoder_1_out5));  // open: Qn, preset, reset
  D_Flip_Flop d_ff_63 (
    .clk(clock_1_out), .D(in_1[0]), .Q(d_ff_63_q[0]), .en(decoder_1_out6));  // open: Qn, preset, reset
  D_Flip_Flop d_ff_64 (
    .clk(clock_1_out), .D(in_1[0]), .Q(d_ff_64_q[0]), .en(decoder_1_out7));  // open: Qn, preset, reset
  Multiplexer #(.select(3), .width(8)) multiplexer_1 (
    .in0(d_ff_57_q), .in1(d_ff_58_q), .in2(d_ff_59_q), .in3(d_ff_60_q), .in4(d_ff_61_q), .in5(d_ff_62_q),
    .in6(d_ff_63_q), .in7(d_ff_64_q), .out(out_4), .sel(in_3));  // open: en
endmodule

module E6 (
  input  [4:0] in_1,
  input  [4:0] in_2,
  input  Enable,
  input  Clear,
  input  [4:0] in_5,
  input  [31:0] in_6,
  output [31:0] out_7,
  output [31:0] out_8
);

  wire and_1_out, and_2_out, and_3_out, and_4_out, and_5_out, and_6_out, and_7_out, and_8_out, and_9_out,
       and_10_out, and_11_out, and_12_out, and_13_out, and_14_out, and_15_out, and_16_out, and_17_out,
       and_18_out, and_19_out, and_20_out, and_21_out, and_22_out, and_23_out, and_24_out, and_25_out,
       and_26_out, and_27_out, and_28_out, and_29_out, and_30_out, and_31_out, and_32_out, clock_1_out,
       decoder_1_out0, decoder_1_out1, decoder_1_out2, decoder_1_out3, decoder_1_out4, decoder_1_out5,
       decoder_1_out6, decoder_1_out7, decoder_1_out8, decoder_1_out9, decoder_1_out10, decoder_1_out11,
       decoder_1_out12, decoder_1_out13, decoder_1_out14, decoder_1_out15, decoder_1_out16, decoder_1_out17,
       decoder_1_out18, decoder_1_out19, decoder_1_out20, decoder_1_out21, decoder_1_out22, decoder_1_out23,
       decoder_1_out24, decoder_1_out25, decoder_1_out26, decoder_1_out27, decoder_1_out28, decoder_1_out29,
       decoder_1_out30, decoder_1_out31, undriven;
  wire [31:0] register_1_q, register_2_q, register_3_q, register_4_q, register_5_q, register_6_q,
       register_7_q, register_8_q, register_9_q, register_10_q, register_11_q, register_12_q, register_13_q,
       register_14_q, register_15_q, register_16_q, register_17_q, register_18_q, register_19_q,
       register_20_q, register_21_q, register_22_q, register_23_q, register_24_q, register_25_q,
       register_26_q, register_27_q, register_28_q, register_29_q, register_30_q, register_31_q,
       register_32_q;

  Decoder #(.select(5)) decoder_1 (
    .out0(decoder_1_out0), .out1(decoder_1_out1), .out2(decoder_1_out2), .out3(decoder_1_out3),
    .out4(decoder_1_out4), .out5(decoder_1_out5), .out6(decoder_1_out6), .out7(decoder_1_out7),
    .out8(decoder_1_out8), .out9(decoder_1_out9), .out10(decoder_1_out10), .out11(decoder_1_out11),
    .out12(decoder_1_out12), .out13(decoder_1_out13), .out14(decoder_1_out14), .out15(decoder_1_out15),
    .out16(decoder_1_out16), .out17(decoder_1_out17), .out18(decoder_1_out18), .out19(decoder_1_out19),
    .out20(decoder_1_out20), .out21(decoder_1_out21), .out22(decoder_1_out22), .out23(decoder_1_out23),
    .out24(decoder_1_out24), .out25(decoder_1_out25), .out26(decoder_1_out26), .out27(decoder_1_out27),
    .out28(decoder_1_out28), .out29(decoder_1_out29), .out30(decoder_1_out30), .out31(decoder_1_out31),
    .sel(in_5));  // open: en
  Clock clock_1 (.out(clock_1_out));
  and and_1 (and_1_out, decoder_1_out0, Enable);
  and and_2 (and_2_out, Enable, decoder_1_out1);
  and and_3 (and_3_out, decoder_1_out2, Enable, undriven);
  and and_4 (and_4_out, decoder_1_out3, Enable);
  and and_5 (and_5_out, decoder_1_out4, Enable);
  and and_6 (and_6_out, decoder_1_out5, Enable);
  and and_7 (and_7_out, decoder_1_out6, Enable);
  and and_8 (and_8_out, decoder_1_out7, Enable);
  and and_9 (and_9_out, decoder_1_out8, Enable);
  and and_10 (and_10_out, decoder_1_out9, Enable);
  and and_11 (and_11_out, decoder_1_out10, Enable);
  and and_12 (and_12_out, decoder_1_out11, Enable);
  and and_13 (and_13_out, decoder_1_out12, Enable);
  and and_14 (and_14_out, decoder_1_out13, Enable);
  and and_15 (and_15_out, decoder_1_out14, Enable);
  and and_16 (and_16_out, decoder_1_out15, Enable);
  and and_17 (and_17_out, decoder_1_out16, Enable);
  and and_18 (and_18_out, decoder_1_out17, Enable);
  and and_19 (and_19_out, decoder_1_out18, Enable);
  and and_20 (and_20_out, decoder_1_out19, Enable);
  and and_21 (and_21_out, decoder_1_out20, Enable);
  and and_22 (and_22_out, decoder_1_out21, Enable);
  and and_23 (and_23_out, decoder_1_out22, Enable);
  and and_24 (and_24_out, decoder_1_out23, Enable);
  and and_25 (and_25_out, decoder_1_out24, Enable);
  and and_26 (and_26_out, decoder_1_out25, Enable);
  and and_27 (and_27_out, decoder_1_out26, Enable);
  and and_28 (and_28_out, decoder_1_out27, Enable);
  and and_29 (and_29_out, decoder_1_out28, Enable);
  and and_30 (and_30_out, decoder_1_out29, Enable);
  and and_31 (and_31_out, decoder_1_out30, Enable);
  and and_32 (and_32_out, Enable, decoder_1_out31);
  Register #(.width(32)) register_1 (.D(in_6), .en(and_1_out), .Q(register_1_q), .clk(clock_1_out), .clr(Clear));
  Register #(.width(32)) register_2 (.D(in_6), .en(and_2_out), .Q(register_2_q), .clk(clock_1_out), .clr(Clear));
  Register #(.width(32)) register_3 (.D(in_6), .en(and_3_out), .Q(register_3_q), .clk(clock_1_out), .clr(Clear));
  Register #(.width(32)) register_4 (.D(in_6), .en(and_4_out), .Q(register_4_q), .clk(clock_1_out), .clr(Clear));
  Register #(.width(32)) register_5 (.D(in_6), .en(and_5_out), .Q(register_5_q), .clk(clock_1_out), .clr(Clear));
  Register #(.width(32)) register_6 (.D(in_6), .en(and_6_out), .Q(register_6_q), .clk(clock_1_out), .clr(Clear));
  Register #(.width(32)) register_7 (.D(in_6), .en(and_7_out), .Q(register_7_q), .clk(clock_1_out), .clr(Clear));
  Register #(.width(32)) register_8 (.D(in_6), .en(and_8_out), .Q(register_8_q), .clk(clock_1_out));  // open: clr
  Register #(.width(32)) register_9 (.D(in_6), .en(and_9_out), .Q(register_9_q), .clk(clock_1_out), .clr(Clear));
  Register #(.width(32)) register_10 (.D(in_6), .en(and_10_out), .Q(register_10_q), .clk(clock_1_out), .clr(Clear));
  Register #(.width(32)) register_11 (.D(in_6), .en(and_11_out), .Q(register_11_q), .clk(clock_1_out), .clr(Clear));
  Register #(.width(32)) register_12 (.D(in_6), .en(and_12_out), .Q(register_12_q), .clk(clock_1_out), .clr(Clear));
  Register #(.width(32)) register_13 (.D(in_6), .en(and_13_out), .Q(register_13_q), .clk(clock_1_out), .clr(Clear));
  Register #(.width(32)) register_14 (.D(in_6), .en(and_14_out), .Q(register_14_q), .clk(clock_1_out), .clr(Clear));
  Register #(.width(32)) register_15 (.D(in_6), .en(and_15_out), .Q(register_15_q), .clk(clock_1_out), .clr(Clear));
  Register #(.width(32)) register_16 (.D(in_6), .en(and_16_out), .Q(register_16_q), .clk(clock_1_out), .clr(Clear));
  Register #(.width(32)) register_17 (.D(in_6), .en(and_17_out), .Q(register_17_q), .clk(clock_1_out), .clr(Clear));
  Register #(.width(32)) register_18 (.D(in_6), .en(and_18_out), .Q(register_18_q), .clk(clock_1_out), .clr(Clear));
  Register #(.width(32)) register_19 (.D(in_6), .en(and_19_out), .Q(register_19_q), .clk(clock_1_out), .clr(Clear));
  Register #(.width(32)) register_20 (.D(in_6), .en(and_20_out), .Q(register_20_q), .clk(clock_1_out), .clr(Clear));
  Register #(.width(32)) register_21 (.D(in_6), .en(and_21_out), .Q(register_21_q), .clk(clock_1_out), .clr(Clear));
  Register #(.width(32)) register_22 (.D(in_6), .en(and_22_out), .Q(register_22_q), .clk(clock_1_out), .clr(Clear));
  Register #(.width(32)) register_23 (.D(in_6), .en(and_23_out), .Q(register_23_q), .clk(clock_1_out), .clr(Clear));
  Register #(.width(32)) register_24 (.D(in_6), .en(and_24_out), .Q(register_24_q), .clk(clock_1_out), .clr(Clear));
  Register #(.width(32)) register_25 (.D(in_6), .en(and_25_out), .Q(register_25_q), .clk(clock_1_out), .clr(Clear));
  Register #(.width(32)) register_26 (.D(in_6), .en(and_26_out), .Q(register_26_q), .clk(clock_1_out), .clr(Clear));
  Register #(.width(32)) register_27 (.D(in_6), .en(and_27_out), .Q(register_27_q), .clk(clock_1_out), .clr(Clear));
  Register #(.width(32)) register_28 (.D(in_6), .en(and_28_out), .Q(register_28_q), .clk(clock_1_out), .clr(Clear));
  Register #(.width(32)) register_29 (.D(in_6), .en(and_29_out), .Q(register_29_q), .clk(clock_1_out), .clr(Clear));
  Register #(.width(32)) register_30 (.D(in_6), .en(and_30_out), .Q(register_30_q), .clk(clock_1_out), .clr(Clear));
  Register #(.width(32)) register_31 (.D(in_6), .en(and_31_out), .Q(register_31_q), .clk(clock_1_out), .clr(Clear));
  Register #(.width(32)) register_32 (.D(in_6), .en(and_32_out), .Q(register_32_q), .clk(clock_1_out), .clr(Clear));
  Multiplexer #(.select(5), .width(32)) multiplexer_1 (
    .in0(register_1_q), .in1(register_2_q), .in2(register_3_q), .in3(register_4_q), .in4(register_5_q),
    .in5(register_6_q), .in6(register_7_q), .in7(register_8_q), .in8(register_9_q), .in9(register_10_q),
    .in10(register_11_q), .in11(register_12_q), .in12(register_13_q), .in13(register_14_q),
    .in14(register_15_q), .in15(register_16_q), .in16(register_17_q), .in17(register_18_q),
    .in18(register_19_q), .in19(register_20_q), .in20(register_21_q), .in21(register_22_q),
    .in22(register_23_q), .in23(register_24_q), .in24(register_25_q), .in25(register_26_q),
    .in26(register_27_q), .in27(register_28_q), .in28(register_29_q), .in29(register_30_q),
    .in30(register_31_q), .in31(register_32_q), .out(out_7), .sel(in_1));  // open: en
  Multiplexer #(.select(5), .width(32)) multiplexer_2 (
    .in0(register_1_q), .in1(register_2_q), .in2(register_3_q), .in3(register_4_q), .in4(register_5_q),
    .in5(register_6_q), .in6(register_7_q), .in7(register_8_q), .in8(register_9_q), .in9(register_10_q),
    .in10(register_11_q), .in11(register_12_q), .in12(register_13_q), .in13(register_14_q),
    .in14(register_15_q), .in15(register_16_q), .in16(register_17_q), .in17(register_18_q),
    .in18(register_19_q), .in19(register_20_q), .in20(register_21_q), .in21(register_22_q),
    .in22(register_23_q), .in23(register_24_q), .in24(register_25_q), .in25(register_26_q),
    .in26(register_27_q), .in27(register_28_q), .in28(register_29_q), .in29(register_30_q),
    .in30(register_31_q), .in31(register_32_q), .out(out_8), .sel(in_2));  // open: en
endmodule

module E7 (
  input  [7:0] A,
  output [7:0] Num1,
  output [7:0] Num2,
  output [7:0] Num3,
  output [7:0] Num4,
  output [7:0] out_6
);

  wire adder_1_cout, adder_2_cout, clock_1_out, full_adder_1_p1;
  wire [1:0] adder_2_out;
  wire [7:0] adder_1_out, adder_3_out;

  Clock clock_1 (.out(clock_1_out));
  _8bit_pipo_register_for_E7 u_8bit_pipo_register_for_e7_1 (.A(A), .out_3(Num1), .Clock(clock_1_out));
  _8bit_pipo_register_for_E7 u_8bit_pipo_register_for_e7_2 (.A(Num1), .out_3(Num2), .Clock(clock_1_out));
  Adder adder_1 (.a(Num2), .b(Num1), .out(adder_1_out), .cin(1'b0), .cout(adder_1_cout));
  _8bit_pipo_register_for_E7 u_8bit_pipo_register_for_e7_3 (.A(Num2), .out_3(Num3), .Clock(clock_1_out));
  Adder adder_2 (.a(adder_1_out), .b(adder_3_out), .out({out_6[5:0], adder_2_out}), .cin(1'b0), .cout(adder_2_cout));
  // FULL_ADDER full_adder_1: pin names not known; wires that end beside it: full_adder_1_p1, adder_2_cout, adder_1_cout, out_6[6], out_6[7]
  _8bit_pipo_register_for_E7 u_8bit_pipo_register_for_e7_4 (.A(Num3), .out_3(Num4), .Clock(clock_1_out));
  Adder adder_3 (.a(Num4), .b(Num3), .out(adder_3_out), .cin(1'b0), .cout(full_adder_1_p1));
endmodule

module _8bit_pipo_register_for_E7 (
  input  Clock,
  input  [7:0] A,
  output [7:0] out_3
);

  D_Flip_Flop d_ff_1 (.clk(Clock), .D(A[7]), .Q(out_3[7]));  // open: Qn, preset, en, reset
  D_Flip_Flop d_ff_2 (.clk(Clock), .D(A[6]), .Q(out_3[6]));  // open: Qn, preset, en, reset
  D_Flip_Flop d_ff_3 (.clk(Clock), .D(A[5]), .Q(out_3[5]));  // open: Qn, preset, en, reset
  D_Flip_Flop d_ff_4 (.clk(Clock), .D(A[4]), .Q(out_3[4]));  // open: Qn, preset, en, reset
  D_Flip_Flop d_ff_5 (.clk(Clock), .D(A[3]), .Q(out_3[3]));  // open: Qn, preset, en, reset
  D_Flip_Flop d_ff_6 (.clk(Clock), .D(A[2]), .Q(out_3[2]));  // open: Qn, preset, en, reset
  D_Flip_Flop d_ff_7 (.clk(Clock), .D(A[1]), .Q(out_3[1]));  // open: Qn, preset, en, reset
  D_Flip_Flop d_ff_8 (.clk(Clock), .D(A[0]), .Q(out_3[0]));  // open: Qn, preset, en, reset
endmodule
