// Logisim project 2101CS88.circ as structural Verilog
module _4_bit_comp_larger (
  input  [3:0] in_1,
  input  [3:0] in_2,
  output [3:0] out_3
);

  wire comparator_1_eq, comparator_1_gt, or_1_out;

  Comparator #(.width(4), .mode("unsigned")) comparator_1 (
    .a(in_1), .b(in_2), .gt(comparator_1_gt), .eq(comparator_1_eq));  // open: lt
  Multiplexer #(.width(4)) multiplexer_1 (.in0(in_2), .in1(in_1), .out(out_3), .sel(or_1_out));  // open: en
  or or_1 (or_1_out, comparator_1_gt, comparator_1_eq);
endmodule

module _4_bit_comp_smaller (
  input  [3:0] in_1,
  input  [3:0] in_2,
  output [3:0] out_3
);

  wire comparator_1_eq, comparator_1_lt, or_1_out;

  Comparator #(.width(4), .mode("unsigned")) comparator_1 (
    .a(in_1), .b(in_2), .eq(comparator_1_eq), .lt(comparator_1_lt));  // open: gt
  Multiplexer #(.width(4)) multiplexer_1 (.in0(in_2), .in1(in_1), .out(out_3), .sel(or_1_out));  // open: en
  or or_1 (or_1_out, comparator_1_eq, comparator_1_lt);
endmodule

module _11bit_smaller (
  input  [15:0] in_1,
  input  [15:0] in_2,
  output [10:0] out_3
);

  wire comparator_1_eq, comparator_1_lt, or_1_out;
  wire [15:11] multiplexer_1_out;

  Comparator #(.width(4), .mode("unsigned")) comparator_1 (
    .a(in_1[14:11]), .b(in_2[14:11]), .eq(comparator_1_eq), .lt(comparator_1_lt));  // open: gt
  Multiplexer #(.width(16)) multiplexer_1 (
    .in0(in_2), .in1(in_1), .out({multiplexer_1_out, out_3}), .sel(or_1_out));  // open: en
  or or_1 (or_1_out, comparator_1_eq, comparator_1_lt);
endmodule

module _11bit_larger (
  input  [15:0] in_1,
  input  [15:0] in_2,
  output [10:0] out_3
);

  wire comparator_1_eq, comparator_1_gt, or_1_out;
  wire [15:11] multiplexer_1_out;

  Comparator #(.width(4), .mode("unsigned")) comparator_1 (
    .a(in_1[14:11]), .b(in_2[14:11]), .gt(comparator_1_gt), .eq(comparator_1_eq));  // open: lt
  Multiplexer #(.width(16)) multiplexer_1 (
    .in0(in_2), .in1(in_1), .out({multiplexer_1_out, out_3}), .sel(or_1_out));  // open: en
  or or_1 (or_1_out, comparator_1_gt, comparator_1_eq);
endmodule

module Floating_point_adder (
  input  [15:0] in_1,
  input  [15:0] in_2,
  input  [3:0] in_3,
  input  [3:0] in_4,
  output [3:0] out_5,
  output [15:0] out_6,
  output [15:0] out_7,
  output Infinity,
  output NaN,
  output zero,
  output Denormalized
);

  wire adder_2_cout, adder_2_out, and_2_out, and_3_out, comparator_1_eq, comparator_1_gt, comparator_1_lt,
       not_1_out, or_1_out, or_2_out, or_3_out, or_4_out, xnor_1_out;
  wire [0:0] adder_4_cout;
  wire [3:0] count_zeroes_1_out_2, n4_bit_comp_larger_1_out_3, n4_bit_comp_smaller_1_out_3, shifter_3_out;
  wire [10:0] n11bit_larger_1_out_3, n11bit_smaller_1_out_3;
  wire [11:11] adder_4_out;
  wire [15:0] adder_1_out, adder_3_out, shifter_1_out, shifter_2_out, subtractor_3_out;
  wire [15:15] shifter_3_out_2;

  _4_bit_comp_larger u_4_bit_comp_larger_1 (.in_1(in_1[14:11]), .in_2(in_2[14:11]), .out_3(n4_bit_comp_larger_1_out_3));
  Multiplexer #(.width(16)) multiplexer_1 (
    .in0(shifter_1_out), .in1(adder_1_out), .out(out_7), .sel(xnor_1_out));  // open: en
  Subtractor #(.width(4)) subtractor_1 (
    .a(n4_bit_comp_larger_1_out_3), .b(n4_bit_comp_smaller_1_out_3), .out(out_5));  // open: bin, bout
  and and_1 (adder_1_out[15], in_2[15], in_1[15]);
  _4_bit_comp_smaller u_4_bit_comp_smaller_1 (
    .in_1(in_1[14:11]), .in_2(in_2[14:11]), .out_3(n4_bit_comp_smaller_1_out_3));
  Adder #(.width(4)) adder_1 (
    .a(n4_bit_comp_larger_1_out_3), .b({out_6[15:13], adder_4_cout[0]}), .out(adder_1_out[14:11]));  // open: cin, cout
  or or_1 (or_1_out, comparator_1_gt, comparator_1_eq);
  Subtractor #(.width(4)) subtractor_2 (
    .a(n4_bit_comp_larger_1_out_3), .b(count_zeroes_1_out_2), .out(shifter_1_out[14:11]));  // open: bin, bout
  Multiplexer multiplexer_2 (.in0(in_1[15]), .in1(in_2[15]), .out(shifter_1_out[15]), .sel(or_1_out));  // open: en
  xnor xnor_1 (xnor_1_out, in_2[15], in_1[15]);
  count_zeroes count_zeroes_1 (.in_1(out_6[10:0]), .out_2(count_zeroes_1_out_2));
  Shifter #(.width(11)) shifter_1 (.in(out_6[10:0]), .\dist (count_zeroes_1_out_2), .out(shifter_1_out[10:0]));
  Shifter #(.width(16), .shift("lr")) shifter_2 (
    .in({1'b0, in_3, n11bit_smaller_1_out_3}), .\dist (out_5), .out(shifter_2_out));
  Comparator #(.width(4)) comparator_1 (
    .a(n4_bit_comp_smaller_1_out_3), .b(n4_bit_comp_larger_1_out_3), .gt(comparator_1_gt),
    .eq(comparator_1_eq), .lt(comparator_1_lt));
  Shifter #(.width(16), .shift("lr")) shifter_3 (
    .in({out_6[15:13], adder_4_cout[0], adder_4_out[11], out_6[10:0]}),
    .\dist ({out_6[15:13], adder_4_cout[0]}), .out({shifter_3_out_2[15], shifter_3_out, adder_1_out[10:0]}));
  _11bit_smaller u_11bit_smaller_1 (.in_1(in_1), .in_2(in_2), .out_3(n11bit_smaller_1_out_3));
  Adder #(.width(1)) adder_2 (
    .a(comparator_1_eq), .b(comparator_1_eq), .out(adder_2_out), .cin(or_2_out), .cout(adder_2_cout));
  or or_2 (or_2_out, comparator_1_gt, comparator_1_lt);
  Subtractor #(.width(16)) subtractor_3 (
    .a({1'b0, in_4, n11bit_larger_1_out_3}), .b(shifter_2_out), .out(subtractor_3_out));  // open: bin, bout
  Multiplexer #(.width(16)) multiplexer_3 (
    .in0(subtractor_3_out), .in1(adder_3_out), .out(out_6), .sel(xnor_1_out));  // open: en
  _11bit_larger u_11bit_larger_1 (.in_1(in_1), .in_2(in_2), .out_3(n11bit_larger_1_out_3));
  Adder #(.width(16)) adder_3 (
    .a({1'b0, in_4, n11bit_larger_1_out_3}), .b(shifter_2_out), .out(adder_3_out));  // open: cin, cout
  Adder #(.width(1)) adder_4 (
    .a(adder_2_out), .b(adder_2_cout), .out(adder_4_out[11]), .cin(out_6[11]), .cout(adder_4_cout[0]));
  or or_3 (or_3_out, out_7[0], out_7[1], out_7[2], out_7[3], out_7[4], out_7[5], out_7[6], out_7[7], out_7[8], out_7[9], out_7[10]);
  and and_2 (and_2_out, out_7[11], out_7[12], out_7[13], out_7[14]);
  or or_4 (or_4_out, out_7[11], out_7[12], out_7[13], out_7[14]);
  Decoder decoder_1 (.out0(Infinity), .out1(NaN), .sel(and_3_out), .en(and_2_out));
  and and_3 (and_3_out, or_3_out, and_2_out);
  not not_1 (not_1_out, or_4_out);
  Decoder decoder_2 (.out0(zero), .out1(Denormalized), .sel(or_3_out), .en(not_1_out));
endmodule

module count_zeroes (
  input  [10:0] in_1,
  output [3:0] out_2
);

  wire [3:0] priority_encoder_1_out;

  Priority_Encoder #(.select(4)) priority_encoder_1 (
    .in0(in_1[0]), .in1(in_1[1]), .in2(in_1[2]), .in3(in_1[3]), .in4(in_1[4]), .in5(in_1[5]), .in6(in_1[6]),
    .in7(in_1[7]), .in8(in_1[8]), .in9(in_1[9]), .in10(in_1[10]), .in11(1'b0), .in12(1'b0), .in13(1'b0),
    .in14(1'b0), .in15(1'b0), .out(priority_encoder_1_out));  // open: gs, en_out, en_in
  Subtractor #(.width(4)) subtractor_1 (.a(4'b1011), .b(priority_encoder_1_out), .out(out_2));  // open: bin, bout
endmodule
